// Digital circuit control_bomba.dig as structural Verilog
module control_bomba (
  input  tanqueH,
  input  tanqueL,
  input  cisternaOK,
  input  cisternaL,
  output bomba
);

  wire rs_ff_as_1_q, rs_ff_as_2_nq;

  RS_FF_AS rs_ff_as_1 (.S(~tanqueL), .R(tanqueH), .Q(rs_ff_as_1_q));  // open: nQ
  RS_FF_AS rs_ff_as_2 (.S(~cisternaL), .R(cisternaOK), .nQ(rs_ff_as_2_nq));  // open: Q
  and and_1 (bomba, rs_ff_as_1_q, rs_ff_as_2_nq);
endmodule
